# Fritzing sketch smart_citizen_board 2 (saved by Fritzing 0.9.2b)
circuit board: 7.8cm x 3.4cm
breadboards: 1

parts:
  D2 = Rectifier Diode [part_number=1N4001 package="300 mil [THT]"]
  R1 = Resistor [tolerance=±5% resistance=100k package=THT]
  3_3V = male pin header, 3 pins [form="♂ (male)"]
  PWR = female pin header, 2 pins [form="♀ (female)"]
  D3 = Rectifier Diode [part_number=1N4001 package="300 mil [THT]"]
  U2 = ESP8266 WiFi Module [part_number=ESP8266]
  CD4048B2 = CD4048B [part_number=CD4050 package="DIP (Dual Inline) [THT]"]
  R8 = Resistor [tolerance=±5% resistance=100k package=THT]
  J-DISC = screw terminal, 8 pins
  Arduino1 = Arduino Pro Mini v13
  EN-PROG = female pin header, 2 pins [form="♀ (female)"]
  J-A5 = screw terminal, 4 pins
  J-GND = screw terminal, 7 pins
  J-VCC = screw terminal, 7 pins

nets:
  N1: D2.cathode, 3_3V.pin1, D3.anode
  N2: D2.anode, PWR.pin2, Arduino1.VCC, J-VCC.pin1, J-VCC.pin2, J-VCC.pin3, J-VCC.pin4, J-VCC.pin5, J-VCC.pin6, J-VCC.pin7
  N3: R1.Pin_0, 3_3V.pin3, D3.cathode
  GND: R1.Pin_1, PWR.pin1, U2.GND, CD4048B2.VSS, R8.Pin_1, Arduino1.GND, J-GND.pin1, J-GND.pin2, J-GND.pin3, J-GND.pin4, J-GND.pin5, J-GND.pin6, J-GND.pin7
  N4: 3_3V.pin2, U2.VCC, U2.GPIO_0, U2.GPIO_2, CD4048B2.J
  N5: U2.RXD, CD4048B2.E
  N6: U2.RST, CD4048B2.C
  N7: U2.CH_PD, R8.Pin_0, EN-PROG.pin2
  N8: U2.TXD, Arduino1.D1/RX
  N9: CD4048B2.Kb, Arduino1.D0/TX
  N10: CD4048B2.Kc, Arduino1.D11_PWM/MOSI
  N11: CD4048B2.Ka, EN-PROG.pin1
  N12: CD4048B2.D, Arduino1.D10_PWM/SS
  N13: J-DISC.pin1, Arduino1.D9_PWM
  N14: J-DISC.pin2, Arduino1.D8
  N15: J-DISC.pin3, Arduino1.D7
  N16: J-DISC.pin4, Arduino1.D6_PWM
  N17: J-DISC.pin5, Arduino1.D5_PWM
  N18: J-DISC.pin6, Arduino1.D4
  N19: J-DISC.pin7, Arduino1.D3_PWM
  N20: J-DISC.pin8, Arduino1.D2
  N21: Arduino1.A3, J-A5.pin1
  N22: Arduino1.A2, J-A5.pin2
  N23: Arduino1.A1, J-A5.pin3
  N24: Arduino1.A0, J-A5.pin4

notes:
  Alex Porto

custom parts:
  ESP8266 WiFi Module: Generic WiFi Module based on the ESP8266 with onboard PCB antenna and UART communications
