# Fritzing sketch smart_citizen_board 4 (saved by Fritzing 0.9.2b)
circuit board: 6.8cm x 3.1cm
breadboards: 1

parts:
  D1 = Rectifier Diode [part_number=1N4001 package="300 mil [THT]"]
  R1 = Resistor [tolerance=±5% resistance=100k package=THT]
  3_3V = male pin header, 3 pins [form="♂ (male)"]
  PWR = female pin header, 2 pins [form="♀ (female)"]
  D2 = Rectifier Diode [part_number=1N4001 package="300 mil [THT]"]
  U2 = ESP8266 WiFi Module [part_number=ESP8266]
  CD4048B2 = CD4048B [part_number=CD4050 package="DIP (Dual Inline) [THT]"]
  R8 = Resistor [tolerance=±5% resistance=100k package=THT]
  Arduino_Pro_Mini = Arduino Pro Mini v13
  EN-PROG = female pin header, 2 pins [form="♀ (female)"]
  J-SENSORS = screw terminal, 4 pins
  J-GND = screw terminal, 7 pins
  J-DISC = screw terminal, 6 pins
  J-VCC = screw terminal, 7 pins

nets:
  N1: D1.cathode, 3_3V.pin1, D2.anode
  N2: D1.anode, PWR.pin2, Arduino_Pro_Mini.VCC, J-VCC.pin1, J-VCC.pin2, J-VCC.pin3, J-VCC.pin4, J-VCC.pin5, J-VCC.pin6, J-VCC.pin7
  N3: R1.Pin_0, 3_3V.pin3, D2.cathode
  GND: R1.Pin_1, PWR.pin1, U2.GND, CD4048B2.VSS, R8.Pin_1, Arduino_Pro_Mini.GND, J-GND.pin1, J-GND.pin2, J-GND.pin3, J-GND.pin4, J-GND.pin5, J-GND.pin6, J-GND.pin7
  N4: 3_3V.pin2, U2.VCC, U2.GPIO_0, U2.GPIO_2, CD4048B2.J
  N5: U2.RXD, CD4048B2.E
  N6: U2.RST, CD4048B2.C
  N7: U2.CH_PD, R8.Pin_0, EN-PROG.pin2
  N8: U2.TXD, Arduino_Pro_Mini.D8
  N9: CD4048B2.Kb, Arduino_Pro_Mini.D9_PWM
  N10: CD4048B2.Kc, Arduino_Pro_Mini.D10_PWM/SS
  N11: CD4048B2.Ka, EN-PROG.pin1
  N12: CD4048B2.D, Arduino_Pro_Mini.D11_PWM/MOSI
  N13: Arduino_Pro_Mini.A3, J-SENSORS.pin1
  N14: Arduino_Pro_Mini.A2, J-SENSORS.pin2
  N15: Arduino_Pro_Mini.A1, J-SENSORS.pin3
  N16: Arduino_Pro_Mini.A0, J-SENSORS.pin4
  N17: Arduino_Pro_Mini.D7, J-DISC.pin1
  N18: Arduino_Pro_Mini.D6_PWM, J-DISC.pin2
  N19: Arduino_Pro_Mini.D5_PWM, J-DISC.pin3
  N20: Arduino_Pro_Mini.D4, J-DISC.pin4
  N21: Arduino_Pro_Mini.D3_PWM, J-DISC.pin5
  N22: Arduino_Pro_Mini.D2, J-DISC.pin6

notes:
  Alex
  Porto
  +
  -
  CC-by-SA

custom parts:
  ESP8266 WiFi Module: Generic WiFi Module based on the ESP8266 with onboard PCB antenna and UART communications
