# Fritzing sketch smart_citizen_board (saved by Fritzing 0.9.2b)
circuit board: 7cm x 6cm
circuit board: 1.5cm x 2.5cm
breadboards: 1

parts:
  D2 = Rectifier Diode [part_number=1N4001 package="300 mil [THT]"]
  R1 = Resistor [tolerance=±5% resistance=100k package=THT]
  3_3V = male pin header, 3 pins [form="♂ (male)"]
  PWR = female pin header, 2 pins [form="♀ (female)"]
  D3 = Rectifier Diode [part_number=1N4001 package="300 mil [THT]"]
  U2 = ESP8266 WiFi Module [part_number=ESP8266]
  CD4048B2 = CD4048B [part_number=CD4050 package="DIP (Dual Inline) [THT]"]
  R4 = Resistor [tolerance=±5% resistance=100k package=THT]
  R5 = Resistor [tolerance=±5% resistance=100k package=THT]
  J-A2 = screw terminal, 3 pins
  R6 = Resistor [tolerance=±5% resistance=100k package=THT]
  R7 = Resistor [tolerance=±5% resistance=100k package=THT]
  J-A4 = screw terminal, 3 pins
  J-A5 = screw terminal, 3 pins
  J-VCC = screw terminal, 5 pins
  J-GND = screw terminal, 5 pins
  R8 = Resistor [tolerance=±5% resistance=100k package=THT]
  EN-PROG = female pin header, 2 pins [form="♀ (female)"]
  J-A3 = screw terminal, 3 pins
  J-DISC = screw terminal, 8 pins
  Arduino1 = Arduino Pro Mini v13

nets:
  N1: D2.cathode, 3_3V.pin1, D3.anode
  N2: D2.anode, PWR.pin2, J-A2.pin3, J-A4.pin3, J-A5.pin3, J-VCC.pin1, J-VCC.pin2, J-VCC.pin3, J-VCC.pin4, J-VCC.pin5, J-A3.pin3, Arduino1.VCC
  N3: R1.Pin_0, 3_3V.pin3, D3.cathode
  GND: R1.Pin_1, PWR.pin1, U2.GND, CD4048B2.VSS, R5.Pin_0, J-A2.pin1, R6.Pin_0, R7.Pin_0, J-A4.pin1, J-A5.pin1, J-GND.pin1, J-GND.pin2, J-GND.pin3, J-GND.pin4, J-GND.pin5, R8.Pin_1, Arduino1.GND
  N4: 3_3V.pin2, U2.VCC, U2.GPIO_0, U2.GPIO_2, CD4048B2.J
  N5: U2.RXD, CD4048B2.E
  N6: U2.RST, CD4048B2.G
  N7: U2.CH_PD, R8.Pin_0, EN-PROG.pin2
  N8: U2.TXD, Arduino1.D1/RX
  N9: CD4048B2.Kd, EN-PROG.pin1
  N10: CD4048B2.H, Arduino1.D11_PWM/MOSI
  N11: CD4048B2.F, Arduino1.D10_PWM/SS
  N12: CD4048B2.Kb, Arduino1.D0/TX
  N13: R4.Pin_0, J-A3.pin1
  N14: R4.Pin_1, J-A3.pin2, Arduino1.A1
  N15: R5.Pin_1, J-A2.pin2, Arduino1.A0
  N16: R6.Pin_1, J-A5.pin2, Arduino1.A3
  N17: R7.Pin_1, J-A4.pin2, Arduino1.A2
  N18: J-DISC.pin1, Arduino1.D9_PWM
  N19: J-DISC.pin2, Arduino1.D8
  N20: J-DISC.pin3, Arduino1.D7
  N21: J-DISC.pin4, Arduino1.D6_PWM
  N22: J-DISC.pin5, Arduino1.D5_PWM
  N23: J-DISC.pin6, Arduino1.D4
  N24: J-DISC.pin7, Arduino1.D3_PWM
  N25: J-DISC.pin8, Arduino1.D2

notes:
  Alex Porto

custom parts:
  ESP8266 WiFi Module: Generic WiFi Module based on the ESP8266 with onboard PCB antenna and UART communications
